# Fritzing sketch wiring (saved by Fritzing 1.0.4)
breadboards: 1

parts:
  LCD1 = LCD screen
  R1 = Resistor [tolerance=±5% power=0.25W resistance=220 package=THT]
  S1 = Pushbutton [package="[THT]"]
  U1 = POT [knob_status=50% power=0.5W package=pot_alpha_rv16af-20]
  J1 = STM32 Nucleo boards
  LED1 = RGB LED (com. cathode, rgb) [color="Red (633nm)" current=0.030A package="5 mm [THT]"]
  SG1 = Buzzer 12mm [part_number=COM-07950 package=buzzer-12mm-ns]
  Part1 = TXB0108 8-channel Bi-directional Logic Level Converter
  LCM1602_IIC1 = LCM1602 IIC [part_number="LCM1602 IIC" chip_label="LCM1602 IIC" package="DIP (Dual Inline) [THT]"]
  R2 = Resistor [tolerance=±5% resistance=220 package="2512 [SMD]"]
  R3 = Resistor [tolerance=±5% resistance=220 package="2512 [SMD]"]
  R4 = Resistor [tolerance=±5% resistance=220 package="2512 [SMD]"]
  TM1638_Led_and_Key1 = TM1638_Led_and_Key [package=THT]

nets:
  VSS: LCD1.VSS, LCM1602_IIC1.VSS
  VDD: LCD1.VDD, LCM1602_IIC1.VDD
  N1: LCD1.V0, LCM1602_IIC1.V0
  N2: LCD1.RS, LCM1602_IIC1.RS
  N3: LCD1.R/W, LCM1602_IIC1.RW
  N4: LCD1.E, LCM1602_IIC1.E
  N5: LCD1.DB0, LCM1602_IIC1.D0
  N6: LCD1.DB1, LCM1602_IIC1.D1
  N7: LCD1.DB2, LCM1602_IIC1.D2
  N8: LCD1.DB3, LCM1602_IIC1.D3
  N9: LCD1.DB4, LCM1602_IIC1.D4
  N10: LCD1.DB5, LCM1602_IIC1.D5
  N11: LCD1.DB6, LCM1602_IIC1.D6
  N12: LCD1.DB7, LCM1602_IIC1.D7
  N13: LCD1.LED+, LCM1602_IIC1.A
  N14: LCD1.LED-, LCM1602_IIC1.K
  N15: R1.Pin_0, S1.Pin_1, S1.Pin_2, U1.A, J1.GND#1188, LED1.green_anode, Part1.B2, LCM1602_IIC1.GND, LCM1602_IIC1.SDA
  N16: R1.Pin_1, SG1.2
  N17: S1.Pin_3, S1.Pin_4, J1.D4
  N18: U1.S, J1.A0
  3V3: U1.E, J1.3V3, Part1.VCCA, TM1638_Led_and_Key1.VCC
  N19: J1.D8, TM1638_Led_and_Key1.STB
  N20: J1.D9_PWM, TM1638_Led_and_Key1.CLK
  N21: J1.D10_PWM/SS, TM1638_Led_and_Key1.DIO
  N22: J1.A4/SDA, Part1.A1
  N23: J1.A5/SCL, Part1.A2
  N24: J1.D2, SG1.1
  N25: J1.D3_PWM, R2.Pin_0
  N26: J1.D5_PWM, R3.Pin_0
  N27: J1.D6_PWM, R4.Pin_0
  5V: J1.5V, Part1.VCCB, LCM1602_IIC1.VCC
  N28: J1.GND#1189, TM1638_Led_and_Key1.GND
  N29: LED1.red_anode, R2.Pin_1
  N30: LED1.common_cathode, R3.Pin_1
  N31: LED1.blue_anode, R4.Pin_1
  N32: Part1.B1, LCM1602_IIC1.SCL

custom parts:
  Buzzer 12mm: Buzzer 12mm Spark Fun Electronics SKU : Comp-Buzzer Through hole This is a small 12mm round speaker that operates around the audible 2kHz range. You can use these speakers to create simple music or user interfaces. This is not a true piezoelectric speaker but behaves similarly. Instead of a piezoelectric crystal that vibrates with an electric current, this tiny speaker uses an electromagnet to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
  TXB0108 8-channel Bi-directional Logic Level Converter: Because the Arduino (and Basic Stamp) are 5V devices, and most modern sensors, displays, flash cards and modes are 3.3V-only, many makers find that they need to perform level shifting/conversion to protect the 3.3V device from 5V. Although one can use resistors to make a divider, for high speed transfers, the resistors can add a lot of slew and cause havoc that is tough to debug. For that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
  LCM1602 IIC: I2C-Module to use a 1602 or 2004 LCD on with the wire.h libory Serial LCD Modul
